# Fritzing sketch SecIOT (saved by Fritzing 0.9.3b)
circuit board: 8.46667cm x 5.64444cm
breadboards: 1

parts:
  R1 = Resistor [tolerance=±5% resistance=1k package=THT]
  R2 = Resistor [tolerance=±5% resistance=1k package=THT]
  R3 = Resistor [tolerance=±5% resistance=1k package=THT]
  INET_STAT = LED - 5mm [color="White (6500K)" package="5 mm [THT]"]
  R4 = Resistor [tolerance=±5% resistance=220 package=THT]
  PWR = LED - 5mm [color="Blue (430nm)" package="5 mm [THT]"]
  R5 = Resistor [tolerance=±5% resistance=220 package=THT]
  TAMPER_STAT = LED - 5mm [color="Green (555nm)" package="5 mm [THT]"]
  R6 = Resistor [tolerance=±5% resistance=220 package=THT]
  LCD = male pin header, 8 pins [form="♂ (male)"]
  Raspberry_Pi_1 = Raspberry Pi 3 [part_number=RPI-3-V1.2]
  U1 = Voltage Regulator - 5V [package="TO220 [THT]"]
  FAC_RESET = Pushbutton [package=THT]
  GUID_SHOW = Pushbutton [package=THT]
  TAMPER = Pushbutton [package=THT]

nets:
  GUID_SHOW_H: R1.Pin_0, GUID_SHOW.leg1
  GND: R1.Pin_1, R2.Pin_1, R3.Pin_1, INET_STAT.anode, PWR.anode, TAMPER_STAT.anode, LCD.pin1, Raspberry_Pi_1.GND, U1.GND
  TAMPER_L: R2.Pin_0, TAMPER.leg1
  FAC_RESET_H: R3.Pin_0, FAC_RESET.leg1
  N1: INET_STAT.cathode, R4.Pin_1
  INET_STAT_H: R4.Pin_0
  N2: PWR.cathode, R5.Pin_1
  3.3V: R5.Pin_0, LCD.pin2, Raspberry_Pi_1.3V3, FAC_RESET.leg0, GUID_SHOW.leg0, TAMPER.leg0
  N3: TAMPER_STAT.cathode, R6.Pin_1
  TAMPER_STAT_H: R6.Pin_0
  LCD_CLK: LCD.pin3, Raspberry_Pi_1.GPIO11
  LCD_DIN: LCD.pin4, Raspberry_Pi_1.GPIO10
  LCD_D/C: LCD.pin5
  LCD_CS: LCD.pin6, Raspberry_Pi_1.GPIO8
  LCD_RST: LCD.pin7
  LCD_BACKLIGHT: LCD.pin8, Raspberry_Pi_1.GPIO24
  5V: Raspberry_Pi_1.5V, U1.output_voltage
  12V: U1.input_voltage

notes:
  Secure Internet of Things Device, Secure IoT Schematic by Andrew Katz, 0.1b
