# Fritzing sketch SecIOT2 (saved by Fritzing 0.9.3b)

parts:
  R1 = Resistor [tolerance=±5% resistance=1k package=THT]
  R2 = Resistor [tolerance=±5% resistance=1k package=THT]
  R3 = Resistor [tolerance=±5% resistance=1k package=THT]
  INET_STAT = LED - 5mm [color="White (6500K)" package="5 mm [THT]"]
  R4 = Resistor [tolerance=±5% resistance=220 package=THT]
  PWR = LED - 5mm [color="Blue (430nm)" package="5 mm [THT]"]
  R5 = Resistor [tolerance=±5% resistance=220 package=THT]
  TAMPER_STAT = LED - 5mm [color="Green (555nm)" package="5 mm [THT]"]
  R6 = Resistor [tolerance=±5% resistance=220 package=THT]
  FAC_RESET = Pushbutton [package=THT]
  GUID_SHOW = Pushbutton [package=THT]
  TAMPER = Pushbutton [package=THT]
  PWR_IN = molex pin header, 2 pins [form=molex]
  LCD = male pin header, 8 pins [form="♂ (male)"]
  Raspberry_Pi/Adafruit_PermaProto = Adafruit Perma-Proto HAT [part_number="Adafruit #2314 and #2310"]

nets:
  GUID_SHOW_H: R1.Pin_0, GUID_SHOW.leg1, Raspberry_Pi/Adafruit_PermaProto.GPIO6
  GND: R1.Pin_1, R2.Pin_1, R3.Pin_1, INET_STAT.anode, PWR.anode, TAMPER_STAT.anode, PWR_IN.pin1, LCD.pin1, Raspberry_Pi/Adafruit_PermaProto.GND, Raspberry_Pi/Adafruit_PermaProto.N$56, Raspberry_Pi/Adafruit_PermaProto.N$59
  TAMPER_L: R2.Pin_0, TAMPER.leg1, Raspberry_Pi/Adafruit_PermaProto.GPIO4
  FAC_RESET_H: R3.Pin_0, FAC_RESET.leg1, Raspberry_Pi/Adafruit_PermaProto.GPIO16
  N1: INET_STAT.cathode, R4.Pin_1
  INET_STAT_H: R4.Pin_0, Raspberry_Pi/Adafruit_PermaProto.GPIO5
  N2: PWR.cathode, R5.Pin_1, Raspberry_Pi/Adafruit_PermaProto.N$57
  3.3V: R5.Pin_0, FAC_RESET.leg0, GUID_SHOW.leg0, TAMPER.leg0, LCD.pin2, Raspberry_Pi/Adafruit_PermaProto.3.3V
  N3: TAMPER_STAT.cathode, R6.Pin_1, Raspberry_Pi/Adafruit_PermaProto.N$61
  TAMPER_STAT_H: R6.Pin_0, Raspberry_Pi/Adafruit_PermaProto.GPIO21
  5V: PWR_IN.pin2, Raspberry_Pi/Adafruit_PermaProto.5.0V
  LCD_CLK: LCD.pin3, Raspberry_Pi/Adafruit_PermaProto.SPI_SCLK
  LCD_DIN: LCD.pin4, Raspberry_Pi/Adafruit_PermaProto.SPI_MOSI
  LCD_D/C: LCD.pin5, Raspberry_Pi/Adafruit_PermaProto.GPIO23
  LCD_CS: LCD.pin6, Raspberry_Pi/Adafruit_PermaProto.SPI_CE0
  LCD_RST: LCD.pin7, Raspberry_Pi/Adafruit_PermaProto.GPIO24
  LCD_BACKLIGHT: LCD.pin8, Raspberry_Pi/Adafruit_PermaProto.GPIO20

custom parts:
  Adafruit Perma-Proto HAT: To kick off the Adafruit HAT party, we have this Perma-Proto inspired plug in daughter board. It has a grid of 0.1" prototyping soldering holes for attaching chips, resistors, LED, potentiometers and more. The holes are connected underneath with traces to mimic the solderless breadboards you're familiar. There's also long power strips for +3V, +5V and Ground connections to the Pi. Near the top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
